// Logisim project trabalho_2.circ as structural Verilog: 1 circuit, main circuit main
module main (
  input  CIN,
  input  B7,
  input  B6,
  input  B5,
  input  B4,
  input  B3,
  input  B2,
  input  B1,
  input  B0,
  input  A7,
  input  A6,
  input  A5,
  input  A4,
  input  A3,
  input  A2,
  input  A1,
  input  A0
);

  wire dip_74283_1_p1, dip_74283_1_p3, dip_74283_1_p4, dip_74283_1_p6, dip_74283_1_p7, dip_74283_1_p8,
       dip_74283_1_p10, dip_74283_1_p11, dip_74283_1_p13, dip_74283_2_p1, dip_74283_2_p2, dip_74283_2_p5,
       dip_74283_2_p8, dip_74283_2_p10, dip_74283_2_p12, dip_74283_2_p13, dip_74283_2_p15;

  LED led_1 (.in(dip_74283_1_p13));
  LED led_2 (.in(dip_74283_1_p10));
  LED led_3 (.in(dip_74283_1_p4));
  LED led_4 (.in(dip_74283_1_p1));
  LED led_5 (.in(dip_74283_2_p15));
  // DIP_74283 dip_74283_1: pin names not known; wires that end beside it: dip_74283_1_p1, A5, dip_74283_1_p3, dip_74283_1_p4, A4, dip_74283_1_p6, dip_74283_1_p7, dip_74283_1_p8, A6, dip_74283_1_p10, dip_74283_1_p11, A7, dip_74283_1_p13
  LED led_6 (.in(dip_74283_2_p1));
  LED led_7 (.in(dip_74283_2_p12));
  LED led_8 (.in(dip_74283_2_p2));
  // DIP_74283 dip_74283_2: pin names not known; wires that end beside it: dip_74283_2_p1, dip_74283_2_p2, dip_74283_2_p1, A1, dip_74283_2_p5, dip_74283_2_p2, A0, dip_74283_2_p8, CIN, dip_74283_2_p10, A2, dip_74283_2_p12, dip_74283_2_p13, A3, dip_74283_2_p15, dip_74283_1_p7
  // DIP_7486 dip_7486_1: pin names not known; wires that end beside it: CIN, B4, dip_74283_1_p6, CIN, B5, dip_74283_1_p3, B7, CIN, dip_74283_1_p11, B6, CIN, dip_74283_1_p8
  // DIP_7486 dip_7486_2: pin names not known; wires that end beside it: CIN, B0, dip_74283_2_p8, CIN, B1, dip_74283_2_p5, B3, CIN, dip_74283_2_p13, B2, CIN, dip_74283_2_p10

  // Notes on the sheet:
  //   S7
  //   S5
  //   S3
  //   S4
  //   S6
  //   Saída
  //   S2
  //   S1
  //   S0
  //   Entrada B
  //   Entrada A
endmodule
